// Digital circuit lab04.dig as structural Verilog
module lab04 (
  input  clk,
  input  rst,
  output [31:0] PC,
  output [5:0] opcode,
  output [4:0] src1__addr,
  output [31:0] src1__out,
  output [4:0] src2__addr,
  output [31:0] src2__out,
  output [4:0] dst__addr,
  output [31:0] dst__data
);

  wire alu_src, branch, mem_read, mem_to_reg, mem_write, PCSrc, reg_dst, reg_write, u_alu_3_zero;
  wire [1:0] alu_op;
  wire [3:0] alu_control;
  wire [4:0] dst_addr1;
  wire [10:0] instr;
  wire [31:0] branchAddr, data_val, imm32, incrPC, mem_addr, multiplexer_1_out, multiplexer_2_out;

  Multiplexer #(.Bits(32)) multiplexer_1 (.sel(PCSrc), .in_0(incrPC), .in_1(branchAddr), .out(multiplexer_1_out));
  gen_register #(.applicationType("IVERILOG"), .CodeFile(".\\gen_register.v")) u_gen_register (
    .clk(clk), .rst(rst), .write_en(clk), .data_in(multiplexer_1_out), .data_out(PC));
  alu #(.applicationType("IVERILOG"), .CodeFile(".\\alu.v")) u_alu (
    .alu_control(4'b0010), .A(PC), .B(32'h4), .result(incrPC));  // open: zero
  RAMDualAccess #(.AddrBits(8), .isProgramMemory("true"), .Bits(32)) cpumemory (
    .str(mem_write), .C(clk), .ld(mem_read), .A1(mem_addr[7:0]), .Din1(src2__out), .A2(PC[9:2]),
    .D1(data_val), .D2({opcode, src1__addr, src2__addr, dst_addr1, instr}));
  alu #(.applicationType("IVERILOG"), .CodeFile(".\\alu.v")) u_alu_2 (
    .alu_control(4'b0010), .A(incrPC), .B({imm32[31:2], 2'b00}), .result(branchAddr));  // open: zero
  BitExtender #(.inputBits(16), .outputBits(32)) bitextender_1 (.in({dst_addr1, instr}), .out(imm32));
  control_unit #(.applicationType("IVERILOG"), .CodeFile(".\\control_unit.v")) u_control_unit (
    .instr_op(opcode), .reg_dst(reg_dst), .branch(branch), .mem_read(mem_read), .mem_to_reg(mem_to_reg),
    .alu_op(alu_op), .mem_write(mem_write), .alu_src(alu_src), .reg_write(reg_write));
  cpu_registers #(.applicationType("IVERILOG"), .CodeFile(".\\cpu_registers.v")) u_cpu_registers (
    .clk(clk), .rst(rst), .write_en(reg_write), .src1_addr(src1__addr), .src2_addr(src2__addr),
    .dst_addr(dst__addr), .data_in(dst__data), .src1_out(src1__out), .src2_out(src2__out));
  alu_control #(.applicationType("IVERILOG"), .CodeFile(".\\alu_control.v")) u_alu_control (
    .alu_op(alu_op), .funct(imm32[5:0]), .alu_control(alu_control));
  Multiplexer #(.Bits(32)) multiplexer_2 (.sel(alu_src), .in_0(src2__out), .in_1(imm32), .out(multiplexer_2_out));
  Multiplexer #(.Bits(5)) multiplexer_3 (.sel(reg_dst), .in_0(src2__addr), .in_1(dst_addr1), .out(dst__addr));
  alu #(.applicationType("IVERILOG"), .CodeFile(".\\alu.v")) u_alu_3 (
    .alu_control(alu_control), .A(src1__out), .B(multiplexer_2_out), .zero(u_alu_3_zero), .result(mem_addr));
  and and_1 (PCSrc, branch, u_alu_3_zero);
  Multiplexer #(.Bits(32)) multiplexer_4 (.sel(mem_to_reg), .in_0(mem_addr), .in_1(data_val), .out(dst__data));

  // Other names for the same wires on the sheet: dst_addr[4:0] = dst__addr;
  //   instr[31:11] = {opcode, src1__addr, src2__addr, dst_addr1}; R2[4:0] = src2__addr; R1[4:0] = src1__addr;
  //   reg_data[31:0] = dst__data; src1_out[31:0] = src1__out; mem_data[31:0] = src2__out; src2_out[31:0] = src2__out

  // Notes on the sheet:
  //   Inputs
  //   PC
  //   Outputs for testing
endmodule
